# Fritzing sketch gps_clock (saved by Fritzing 0.9.5d)
breadboards: 1

parts:
  Компонент1 = Arduino Nano (Rev3.0)
  YwRobot_Power_Supply1 = YwRobot Breadboard Power Supply [part_number=545043]
  Компонент2 = u-blox NEO-6M GPS Breakout
  A1 = lcd color display 1.3in 240x240 7pin interface [package=THT]
  S1 = Pushbutton [package="[SMD]"]

nets:
  GND: Компонент1.GND, YwRobot_Power_Supply1.GND#11, YwRobot_Power_Supply1.GND#12, Компонент2.GND, A1.GND
  N1: Компонент1.D2, Компонент2.TXD
  N2: Компонент1.D3, Компонент2.RXD
  N3: Компонент1.D5, A1.DC
  N4: Компонент1.D6, A1.RES
  N5: Компонент1.D7, S1.Pin_3, S1.Pin_4
  N6: Компонент1.D11/MOSI, A1.SCL
  VIN: Компонент1.VIN, YwRobot_Power_Supply1.VCC#9, YwRobot_Power_Supply1.VCC#10, Компонент2.VCC
  N7: Компонент1.D13/SCK, A1.SDA
  N8: YwRobot_Power_Supply1.VCC#5, YwRobot_Power_Supply1.VCC#6, A1.VCC
  N9: YwRobot_Power_Supply1.GND#13, YwRobot_Power_Supply1.GND#14
  N10: S1.Pin_1, S1.Pin_2

custom parts:
  YwRobot Breadboard Power Supply: The YwRobot Breadboard Power Supply (MB-V2) has two power rails; they can be 5V or 3V3. Power to the module can be provided through the female USB socket or through the A10 (female) 2.1mm power jack.
  lcd color display 1.3in 240x240 7pin interface: 1.3 Inch Color 240 x 240 IPS TFT LCD Display Screen Module Board 7 Pin 4 Wire ST7789VW Drive IC SPI interface.
